# Fritzing sketch Device1_Schematic_Main_Board (saved by Fritzing 0.8.7b)
circuit board: 16.9333cm x 5.64444cm
breadboards: 1

parts:
  Pi1 = Adafruit Pi Cobbler
  PIR1 = PIR sensor
  Raspberry_Pi_rev1 = Raspberry Pi B rev2  # not connected
  Nokia_5110_LCD_Module1 = Nokia5110LCDModule
  S1 = Pushbutton [package="[THT]"]
  S2 = Reed switch [package=THT]
  J1 = Piezo Speaker
  LED1 = LED - 3mm [color="Red (633nm)" package="3 mm [THT]"]
  R1 = Resistor [tolerance=±5% resistance=220k package=THT]

nets:
  N1: Pi1.3V3, Nokia_5110_LCD_Module1.6_DN_(MOSI), LED1.anode
  N2: Pi1.5V0, PIR1.VDD
  GND: Pi1.GND, PIR1.GND, Nokia_5110_LCD_Module1.LED, S1.Pin_1, S1.Pin_2, S2.pin_2, J1.pin1
  N3: Pi1.#4, PIR1.SIG
  N4: Pi1.#17, S2.pin_1
  N5: Pi1.#18, Nokia_5110_LCD_Module1.SCLK
  N6: Pi1.#21, J1.pin2
  N7: Pi1.#22, S1.Pin_3, S1.Pin_4
  N8: Pi1.#23, Nokia_5110_LCD_Module1.SCE
  N9: Pi1.#24, Nokia_5110_LCD_Module1.Vcc
  N10: Pi1.MOSI, Nokia_5110_LCD_Module1.RST
  N11: Pi1.#25, R1.Pin_1
  N12: Pi1.SCLK, Nokia_5110_LCD_Module1.D/C
  N13: Pi1.CE0, Nokia_5110_LCD_Module1.Grnd
  N14: LED1.cathode, R1.Pin_0

custom parts:
  Adafruit Pi Cobbler: Adafruit Pi Cobbler GPIO Breakout for Raspberry Pi
  : Nokia 5110 LCD with 8 pin. It's a 45mm*45mm module part. Description: The Nokia 5110 is a basic graphic LCD screen for lots of applications. It was originally intended for as a cell phone screen. This one is mounted on an easy to solder PCB. It uses the PCD8544 controller. The PCD8544 is a low power CMOS LCD controller/driver, designed to drive a graphic display of 48 rows and 84 columns. All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
