# Fritzing sketch Device2_Schematic_Kitchen_PowerMeter (saved by Fritzing 0.8.7b)
circuit board: 8.46667cm x 5.64444cm
breadboards: 1

parts:
  IC1 = MCP3008 8-channel 10-bit ADC [part_number=MCP3008]
  Pi1 = Adafruit Pi Cobbler
  L2 = Non-Invasive Current Sensor [package="1206 [SMD]"]
  C1 = Ceramic Capacitor [capacitance=330nF part_number="330nK MMK BX2 63-" package="100 mil [THT, multilayer]"]
  C2 = Electrolytic Capacitor [capacitance=10μF package="0605 [SMD, electrolytic]"]
  R2 = Resistor [tolerance=±5% resistance=10k package=THT]
  R3 = Resistor [tolerance=±5% resistance=10k package=THT]
  R4 = Resistor [tolerance=±5% resistance=1k part_number=Lower-MoreTolerance package=THT]

nets:
  N1: IC1.no_name_yet#1, L2.pin_K, R4.Pin_0
  N2: IC1.no_name_yet#9, IC1.no_name_yet#14, Pi1.GND, C1.0, C2.+, R2.Pin_1
  N3: IC1.no_name_yet#10, Pi1.#25
  N4: IC1.no_name_yet#11, Pi1.#24
  N5: IC1.no_name_yet#12, Pi1.#23
  N6: IC1.no_name_yet#13, Pi1.#18
  N7: IC1.no_name_yet#15, IC1.no_name_yet#16, Pi1.3V3, C1.1, R3.Pin_1
  N8: L2.pin_L, C2.-, R2.Pin_0, R3.Pin_0, R4.Pin_1

custom parts:
  Adafruit Pi Cobbler: Adafruit Pi Cobbler GPIO Breakout for Raspberry Pi
