# Fritzing sketch Device3_Schematic_LivingRoom (saved by Fritzing 0.9.0b)
breadboards: 1

parts:
  Pi1 = Adafruit Pi Cobbler
  DHT1 = DHT11 Humitidy and Temperature Sensor
  IC1 = MCP23017 I2C I/O Expander  # not connected
  R1 = Resistor [tolerance=±5% resistance=10k package="1206 [SMD]"]
  IC2 = MCP3008 8-channel 10-bit ADC [part_number=MCP3008]
  Part1 = Gas Sensor Breakout Board
  Part2 = Breakout Board for Electret Microphone  # not connected
  LUX1 = Flora Lux Sensor

nets:
  3V3: Pi1.3V3, DHT1.VDD, R1.Pin_0, IC2.no_name_yet#7, IC2.no_name_yet#8, Part1.H1, LUX1.3v3
  N1: Pi1.SDA0, LUX1.sda2
  N2: Pi1.SCL0, LUX1.scl2
  GND: Pi1.GND, DHT1.GND, IC2.no_name_yet#1, IC2.no_name_yet#6, Part1.GND, LUX1.gnd
  N3: Pi1.#4, DHT1.DATA, R1.Pin_1
  N4: Pi1.#18, IC2.no_name_yet#5
  N5: Pi1.#23, IC2.no_name_yet#4
  N6: Pi1.#24, IC2.no_name_yet#3
  N7: Pi1.#25, IC2.no_name_yet#2
  N8: IC2.no_name_yet#9, Part1.A1

custom parts:
  Adafruit Pi Cobbler: Adafruit Pi Cobbler GPIO Breakout for Raspberry Pi
  DHT11 Humitidy and Temperature Sensor: DHT11 Humidity and Temperature Sensor
  MCP23017 I2C I/O Expander: MCP23017 I2C 16-Channel I/O Expander
  Flora Lux Sensor: Adafruit Flora TSL2561 Lux Sensor
